# Fritzing sketch lcd-clock (saved by Fritzing 0.8.5b)
breadboards: 1

parts:
  POT1 = Breadboard Trimpot
  GPS1 = Adafruit Ultimate GPS Breakout
  LCD1 = LCD screen
  Part1 = Arduino Nano (Rev3.0)

nets:
  VSS: POT1.PIN1, LCD1.VSS, LCD1.R/W, LCD1.LED+, LCD1.LED-, Part1.GND
  N1: POT1.PIN2, LCD1.V0
  VIN: POT1.PIN3, GPS1.VIN, LCD1.VDD, Part1.5V
  N2: GPS1.TX, Part1.D3
  N3: GPS1.RX, Part1.D2
  N4: LCD1.RS, Part1.D7
  N5: LCD1.E, Part1.D8
  N6: LCD1.DB4, Part1.D9
  N7: LCD1.DB5, Part1.D10
  N8: LCD1.DB6, Part1.D11/MOSI
  N9: LCD1.DB7, Part1.D12/MISO
