# Fritzing sketch one-digit (saved by Fritzing 0.8.5b)
breadboards: 1

parts:
  Part1 = Arduino Micro (Rev3)
  U1 = 7-SEGMENT-DISPLAY-1_-RED [package=7-segment-1_pth]
  R1 = Resistor [tolerance=±5% resistance=10k package=THT]
  R2 = Resistor [tolerance=±5% resistance=10k package=THT]
  R3 = Resistor [tolerance=±5% resistance=10k package=THT]
  R4 = Resistor [tolerance=±5% resistance=10k package=THT]
  R5 = Resistor [tolerance=±5% resistance=10k package=THT]
  R6 = Resistor [tolerance=±5% resistance=10k package=THT]
  R7 = Resistor [tolerance=±5% resistance=10k package=THT]
  R8 = Resistor [tolerance=±5% resistance=10k package=THT]
  GPS1 = Adafruit Ultimate GPS Breakout

nets:
  GND: Part1.GND, U1.G1, U1.G2, GPS1.GND
  N1: Part1.D2/SDA, GPS1.RX
  N2: Part1.D3/SCL, GPS1.TX
  N3: Part1.D5_PWM, R7.Pin_1
  N4: Part1.D6_PWM/A7, R8.Pin_1
  N5: Part1.D7, R3.Pin_1
  N6: Part1.D8_PWM/A8, R2.Pin_1
  N7: Part1.D9_PWM/A9, R1.Pin_1
  N8: Part1.D10_PWM/A10, R6.Pin_1
  N9: Part1.D11_PWM, R5.Pin_1
  N10: Part1.D12_PWM/A11, R4.Pin_1
  5V: Part1.5V, GPS1.VIN
  N11: U1.E, R1.Pin_0
  N12: U1.D, R2.Pin_0
  N13: U1.C, R3.Pin_0
  N14: U1.DP, R4.Pin_0
  N15: U1.B, R8.Pin_0
  N16: U1.A, R7.Pin_0
  N17: U1.F, R6.Pin_0
  N18: U1.G, R5.Pin_0
